// Logisim project G1.1.circ as structural Verilog
module NOT (
  input  A,
  output B
);

  nor nor_1 (B, A, A);
endmodule

module OR (
  input  A,
  input  B,
  output C
);

  wire nor_1_out;

  nor nor_1 (nor_1_out, A, B);
  NOT NOT (.A(nor_1_out), .B(C));
endmodule

module AND (
  input  A,
  input  B,
  output C
);

  wire NOT_2_b, NOT_b;

  NOT NOT (.A(A), .B(NOT_b));
  NOT NOT_2 (.A(B), .B(NOT_2_b));
  nor nor_1 (C, NOT_b, NOT_2_b);
endmodule

module XOR (
  input  A,
  input  B,
  output C
);

  wire AND_c, nor_1_out;

  nor nor_1 (nor_1_out, A, B);
  AND AND (.A(A), .B(B), .C(AND_c));
  nor nor_2 (C, nor_1_out, AND_c);
endmodule
