// Logisim project G1.2.circ as structural Verilog: 8 circuits, main circuit main
module main (
  input  [3:0] ALUOperation,
  input  [3:0] A,
  input  [3:0] B,
  input  [3:0] ALUOperation_2,
  output Zero,
  output [3:0] Result,
  output Overflow
);

  wire and_1_out, and_2_out, and_3_out, clock_1_out, comparator_1_eq, comparator_2_eq, mips_alu_4_bit_1_p4,
       mips_alu_4_bit_1_p6, multiplexer_1_out, n4bit_alu_2_overflow, n4bit_alu_2_zero, not_1_out, not_2_out,
       xnor_1_out;
  wire [3:0] mips_alu_4_bit_1_p5, n4bit_alu_2_result, random_1_out, random_2_out;

  Clock clock_1 (.out(clock_1_out));
  Random #(.width(4)) random_1 (.clk(clock_1_out), .next(multiplexer_1_out), .out(random_1_out));  // open: clr
  Random #(.width(4), .seed(1)) random_2 (
    .clk(clock_1_out), .next(multiplexer_1_out), .out(random_2_out));  // open: clr
  _4bit_ALU u_4bit_alu_1 (.A(A), .B(B), .Operation(ALUOperation), .Zero(Zero), .Result(Result), .Overflow(Overflow));
  _4bit_ALU u_4bit_alu_2 (
    .A(random_1_out), .B(random_2_out), .Operation(ALUOperation_2), .Zero(n4bit_alu_2_zero),
    .Result(n4bit_alu_2_result), .Overflow(n4bit_alu_2_overflow));
  // MIPS_ALU_4_bit mips_alu_4_bit_1: pin names not known; wires that end beside it: random_1_out, random_2_out, ALUOperation_2, mips_alu_4_bit_1_p4, mips_alu_4_bit_1_p5, mips_alu_4_bit_1_p6
  not not_1 (not_1_out, ALUOperation_2[0]);
  and and_1 (and_1_out, not_1_out, ALUOperation_2[1]);
  xnor xnor_1 (xnor_1_out, n4bit_alu_2_zero, mips_alu_4_bit_1_p4);
  and and_2 (and_2_out, xnor_1_out, comparator_1_eq);
  Comparator #(.width(4)) comparator_1 (
    .a(n4bit_alu_2_result), .b(mips_alu_4_bit_1_p5), .eq(comparator_1_eq));  // open: gt, lt
  and and_3 (and_3_out, comparator_1_eq, comparator_2_eq);
  Comparator #(.width(1)) comparator_2 (
    .a(n4bit_alu_2_overflow), .b(mips_alu_4_bit_1_p6), .eq(comparator_2_eq));  // open: gt, lt
  Multiplexer #(.enable("false")) multiplexer_1 (
    .in0(and_2_out), .in1(and_3_out), .out(multiplexer_1_out), .sel(and_1_out));
  not not_2 (not_2_out, multiplexer_1_out);
  LED led_1 (.in(not_2_out));

  // Notes on the sheet:
  //   Manual test
  //   Automatic test
  //   Black box ALU
  //   Stop generating new examples on error
  //   Only compare overflow bit on add or subtract
  //   Black = ok
  //   Red = error
endmodule

module _4bit_ALU (
  input  [3:0] A,
  input  [3:0] B,
  input  [3:0] Operation,
  output Zero,
  output [3:0] Result,
  output Overflow
);

  wire n1bit_alu_1_carryout, n1bit_alu_2_carryout, n1bit_alu_3_carryout, n1bit_alu_last_1_set;

  nor nor_1 (Zero, Result[0], Result[1], Result[2], Result[3]);
  _1bit_ALU u_1bit_alu_1 (
    .A(A[0]), .B(B[0]), .Less(n1bit_alu_last_1_set), .Result(Result[0]), .Ainvert(Operation[3]),
    .Binvert(Operation[2]), .CarryIn(Operation[2]), .Operation(Operation[1:0]),
    .CarryOut(n1bit_alu_1_carryout));
  _1bit_ALU u_1bit_alu_2 (
    .A(A[1]), .B(B[1]), .Less(1'b0), .Result(Result[1]), .Ainvert(Operation[3]), .Binvert(Operation[2]),
    .CarryIn(n1bit_alu_1_carryout), .Operation(Operation[1:0]), .CarryOut(n1bit_alu_2_carryout));
  _1bit_ALU u_1bit_alu_3 (
    .A(A[2]), .B(B[2]), .Less(1'b0), .Result(Result[2]), .Ainvert(Operation[3]), .Binvert(Operation[2]),
    .CarryIn(n1bit_alu_2_carryout), .Operation(Operation[1:0]), .CarryOut(n1bit_alu_3_carryout));
  _1bit_ALU_last u_1bit_alu_last_1 (
    .Binvert(Operation[2]), .Ainvert(Operation[3]), .CarryIn(n1bit_alu_3_carryout),
    .Operation(Operation[1:0]), .A(A[3]), .Result(Result[3]), .B(B[3]), .Less(1'b0),
    .Set(n1bit_alu_last_1_set), .Overflow(Overflow));

  // Other names for the same wires on the sheet: Operation_t[1:0] = Operation[1:0]; Binvert = Operation[2];
  //   Ainvert = Operation[3]
endmodule

module _1bit_ALU (
  input  Binvert,
  input  Ainvert,
  input  CarryIn,
  input  [1:0] Operation,
  input  A,
  input  B,
  input  Less,
  output Result,
  output CarryOut
);

  wire and_1_out, n1bit_full_adder_1_sum, n1bit_multiplexer_1_c, n1bit_multiplexer_2_c, not_1_out, not_2_out,
       or_1_out;

  _1bit_multiplexer u_1bit_multiplexer_1 (.A(A), .B(not_1_out), .C(n1bit_multiplexer_1_c), .S(Ainvert));
  not not_1 (not_1_out, A);
  not not_2 (not_2_out, B);
  _1bit_multiplexer u_1bit_multiplexer_2 (.A(B), .B(not_2_out), .C(n1bit_multiplexer_2_c), .S(Binvert));
  and and_1 (and_1_out, n1bit_multiplexer_1_c, n1bit_multiplexer_2_c);
  or or_1 (or_1_out, n1bit_multiplexer_1_c, n1bit_multiplexer_2_c);
  _1bit_full_adder u_1bit_full_adder_1 (
    .A(n1bit_multiplexer_1_c), .B(n1bit_multiplexer_2_c), .Sum(n1bit_full_adder_1_sum), .CarryOut(CarryOut),
    .CarryIn(CarryIn));
  _2bit_multiplexer u_2bit_multiplexer_1 (
    ._00(and_1_out), ._01(or_1_out), ._10(n1bit_full_adder_1_sum), ._11(Less), .R(Result), .S(Operation));
endmodule

module _2bit_multiplexer (
  input  [1:0] S,
  input  _00,
  input  _01,
  input  _10,
  input  _11,
  output R
);

  wire and_1_out, and_2_out, and_3_out, and_4_out, decoder__00, decoder__01, decoder__10, decoder__11;

  _2bit_decoder decoder (.in_1(S), ._00(decoder__00), ._01(decoder__01), ._10(decoder__10), ._11(decoder__11));
  and and_1 (and_1_out, decoder__00, _00);
  and and_2 (and_2_out, decoder__01, _01);
  and and_3 (and_3_out, decoder__10, _10);
  and and_4 (and_4_out, decoder__11, _11);
  or or_1 (R, and_4_out, and_3_out, and_2_out, and_1_out);
endmodule

module _2bit_decoder (
  input  [1:0] in_1,
  output _00,
  output _01,
  output _10,
  output _11
);

  and and_1 (_00, ~in_1[0], ~in_1[1]);  // AND_Gate
  and and_2 (_01, in_1[0], ~in_1[1]);  // AND_Gate
  and and_3 (_10, ~in_1[0], in_1[1]);  // AND_Gate
  and and_4 (_11, in_1[0], in_1[1]);
endmodule

module _1bit_full_adder (
  input  A,
  input  B,
  input  CarryIn,
  output Sum,
  output CarryOut
);

  wire and_1_out, and_2_out, xor_1_out;

  xor xor_1 (xor_1_out, A, B);
  and and_1 (and_1_out, xor_1_out, CarryIn);
  and and_2 (and_2_out, B, A);
  xor xor_2 (Sum, xor_1_out, CarryIn);
  or or_1 (CarryOut, and_1_out, and_2_out);
endmodule

module _1bit_multiplexer (
  input  S,
  input  A,
  input  B,
  output C
);

  wire and_1_out, and_2_out;

  and and_1 (and_1_out, ~S, A);  // AND_Gate
  or or_1 (C, and_1_out, and_2_out);
  and and_2 (and_2_out, S, B);
endmodule

module _1bit_ALU_last (
  input  Binvert,
  input  Ainvert,
  input  CarryIn,
  input  [1:0] Operation,
  input  A,
  input  B,
  input  Less,
  output Result,
  output Set,
  output Overflow
);

  wire and_1_out, n1bit_full_adder_1_carryout, n1bit_full_adder_1_sum, n1bit_multiplexer_1_c,
       n1bit_multiplexer_2_c, not_1_out, not_2_out, or_1_out;

  not not_1 (not_1_out, A);
  _1bit_multiplexer u_1bit_multiplexer_1 (.A(A), .B(not_1_out), .C(n1bit_multiplexer_1_c), .S(Ainvert));
  _1bit_multiplexer u_1bit_multiplexer_2 (.A(B), .B(not_2_out), .C(n1bit_multiplexer_2_c), .S(Binvert));
  not not_2 (not_2_out, B);
  and and_1 (and_1_out, n1bit_multiplexer_1_c, n1bit_multiplexer_2_c);
  or or_1 (or_1_out, n1bit_multiplexer_1_c, n1bit_multiplexer_2_c);
  _1bit_full_adder u_1bit_full_adder_1 (
    .A(n1bit_multiplexer_1_c), .B(n1bit_multiplexer_2_c), .Sum(n1bit_full_adder_1_sum),
    .CarryOut(n1bit_full_adder_1_carryout), .CarryIn(CarryIn));
  _2bit_multiplexer u_2bit_multiplexer_1 (
    ._00(and_1_out), ._01(or_1_out), ._10(n1bit_full_adder_1_sum), ._11(Less), .R(Result), .S(Operation));
  xor xor_1 (Overflow, CarryIn, n1bit_full_adder_1_carryout);
  xor xor_2 (Set, n1bit_full_adder_1_sum, Overflow);
endmodule
