// Logisim project file.circ as structural Verilog: 5 circuits, main circuit main
module main (
  input  in_1
);

  wire ALU_Zero, ALUSrc, and_1_out, and_2_out, and_3_out, Branch, Clock, is_sw, Jump, MemRead, MemToReg,
       MemWrite, mips_alu_2_p4, not_1_out, not_2_out, not_3_out, not_4_out, RegDst, RegToPC, RegWrite,
       Run_Instr, Should_Branch, Write_To_Reg, ZeroInvert;
  wire [1:0] ALUOp;
  wire [3:0] mips_alu_2_p3;
  wire [4:0] instr_rW, lw_rW, multiplexer_3_out_2, multiplexer_3_out_3, multiplexer_5_out, multiplexer_6_out;
  wire [5:0] instr__0_5;
  wire [15:6] multiplexer_3_out;
  wire [27:0] shifter_2_out;
  wire [31:0] ALU_Result, bit_extender_1_out, lw_sw_Addr, mips_alu_2_p5, mips_alu_3_p4, multiplexer_1_out,
       multiplexer_2_out, multiplexer_4_out, multiplexer_8_out, multiplexer_10_out, multiplexer_12_out,
       multiplexer_13_out, PC_4, ram_1_data, Reg_A_Value, Reg_B_Value, register_1_q, shifter_1_out,
       shifter_3_out, sw_Data;
  wire [31:26] multiplexer_3_out_4;

  Multiplexer #(.width(32), .enable("false")) multiplexer_1 (
    .in0(multiplexer_13_out), .in1({32{1'b0}}), .out(multiplexer_1_out), .sel(in_1));
  Register #(.width(32)) register_1 (
    .D(multiplexer_1_out), .en(Run_Instr), .Q(register_1_q), .clk(Clock));  // open: clr
  and and_1 (and_1_out, ~MemRead, ~MemWrite);  // AND_Gate
  Multiplexer #(.width(32), .enable("false")) multiplexer_2 (
    .in0(lw_sw_Addr), .in1(register_1_q), .out(multiplexer_2_out), .sel(Run_Instr));
  Shifter #(.width(32), .shift("lr")) shifter_1 (.in(multiplexer_2_out), .\dist (5'b00010), .out(shifter_1_out));
  Register #(.width(1)) Run_Instr_Next (.D(and_1_out), .Q(Run_Instr), .clk(Clock));  // open: en, clr
  Register #(.width(1)) Is_Store (.D(MemWrite), .Q(is_sw), .clk(Clock));  // open: en, clr
  Register #(.width(32)) u_sw_Data (.D(Reg_B_Value), .Q(sw_Data), .clk(Clock));  // open: en, clr
  Register #(.width(32)) Addr (.D(ALU_Result), .Q(lw_sw_Addr), .clk(Clock));  // open: en, clr
  Register #(.width(5)) u_lw_rW (.D(instr_rW), .Q(lw_rW), .clk(Clock));  // open: en, clr
  Clock clock_1 (.out(Clock));
  RAM #(.addrWidth(24), .dataWidth(32), .bus("separate")) ram_1 (
    .addr(shifter_1_out[23:0]), .din(sw_Data), .data(ram_1_data), .str(is_sw), .clk(Clock));  // open: sel, ld, clr
  // MIPS_ALU mips_alu_1: pin names not known; wires that end beside it: register_1_q, 32'h4, 4'b0010, PC_4
  Multiplexer #(.width(32), .enable("false")) multiplexer_3 (
    .in0({32{1'b0}}), .in1(ram_1_data),
    .out({multiplexer_3_out_4, multiplexer_3_out_3, multiplexer_3_out_2, multiplexer_3_out, instr__0_5}),
    .sel(Run_Instr));
  and and_2 (and_2_out, RegWrite, Run_Instr);
  and and_3 (and_3_out, ~Run_Instr, ~is_sw);  // AND_Gate
  Multiplexer #(.width(32), .enable("false")) multiplexer_4 (
    .in0(ram_1_data), .in1(ALU_Result), .out(multiplexer_4_out), .sel(Run_Instr));
  or or_1 (Write_To_Reg, and_2_out, and_3_out);
  Shifter #(.width(28)) shifter_2 (
    .in({2'b00, multiplexer_3_out_3, multiplexer_3_out_2, multiplexer_3_out, instr__0_5}), .\dist (5'b00010),
    .out(shifter_2_out));
  Multiplexer #(.width(5), .enable("false")) multiplexer_5 (
    .in0(lw_rW), .in1(multiplexer_6_out), .out(multiplexer_5_out), .sel(Run_Instr));
  Multiplexer #(.width(5), .enable("false")) multiplexer_6 (
    .in0(instr_rW), .in1({5{1'b1}}), .out(multiplexer_6_out), .sel(Jump));
  Multiplexer #(.width(5), .enable("false")) multiplexer_7 (
    .in0(multiplexer_3_out_2), .in1(multiplexer_3_out[15:11]), .out(instr_rW), .sel(RegDst));
  assign bit_extender_1_out = {{16{multiplexer_3_out[15]}}, {multiplexer_3_out, instr__0_5}};  // Bit_Extender bit_extender_1
  // RegisterFile registerfile_1: pin names not known; wires that end beside it: multiplexer_4_out, Clock, Write_To_Reg, multiplexer_5_out, multiplexer_3_out_3, multiplexer_3_out_2, in_1, Reg_A_Value, Reg_B_Value
  Control control_1 (
    .Instruction_31_26(multiplexer_3_out_4), .RegDst(RegDst), .ALUsrc(ALUSrc), .MemtoReg(MemToReg),
    .RegWrite(RegWrite), .MemRead(MemRead), .MemWrite(MemWrite), .Branch(Branch), .ALUOp(ALUOp), .Jump(Jump),
    .ZeroInvert(ZeroInvert));
  Multiplexer #(.width(32), .enable("false")) multiplexer_8 (
    .in0(bit_extender_1_out), .in1(Reg_B_Value), .out(multiplexer_8_out), .sel(not_1_out));
  not not_1 (not_1_out, ALUSrc);
  Shifter #(.width(32)) shifter_3 (.in(bit_extender_1_out), .\dist (5'b00010), .out(shifter_3_out));
  // MIPS_ALU mips_alu_2: pin names not known; wires that end beside it: Reg_A_Value, multiplexer_8_out, mips_alu_2_p3, mips_alu_2_p4, mips_alu_2_p5
  and and_4 (Should_Branch, ALU_Zero, Branch);
  // MIPS_ALU mips_alu_3: pin names not known; wires that end beside it: PC_4, shifter_3_out, 4'b0010, mips_alu_3_p4
  Multiplexer #(.enable("false")) multiplexer_9 (
    .in0(mips_alu_2_p4), .in1(not_2_out), .out(ALU_Zero), .sel(ZeroInvert));
  not not_2 (not_2_out, mips_alu_2_p4);
  ALU_control alu_control_1 (.ALUOp(ALUOp), .Funct(instr__0_5), .ALUctrl(mips_alu_2_p3), .RegtoPC(RegToPC));
  Multiplexer #(.width(32), .enable("false")) multiplexer_10 (
    .in0(PC_4), .in1(mips_alu_3_p4), .out(multiplexer_10_out), .sel(Should_Branch));
  Multiplexer #(.width(32), .enable("false")) multiplexer_11 (
    .in0(mips_alu_2_p5), .in1(PC_4), .out(ALU_Result), .sel(Jump));
  Multiplexer #(.width(32), .enable("false")) multiplexer_12 (
    .in0({PC_4[31:28], shifter_2_out}), .in1(multiplexer_10_out), .out(multiplexer_12_out), .sel(not_4_out));
  not not_3 (not_3_out, RegToPC);
  not not_4 (not_4_out, Jump);
  Multiplexer #(.width(32), .enable("false")) multiplexer_13 (
    .in0(Reg_A_Value), .in1(multiplexer_12_out), .out(multiplexer_13_out), .sel(not_3_out));

  // Other names for the same wires on the sheet: Reset = in_1

  // Notes on the sheet:
  //   PC
endmodule

module Control (
  input  [5:0] Instruction_31_26,
  output RegDst,
  output ALUsrc,
  output MemtoReg,
  output RegWrite,
  output MemRead,
  output MemWrite,
  output Branch,
  output [1:0] ALUOp,
  output Jump,
  output ZeroInvert
);

  // PLA Control: pin names not known; wires that end beside it: Instruction_31_26, {ZeroInvert, Jump, RegDst, ALUsrc, MemtoReg, RegWrite, MemRead, MemWrite, Branch, ALUOp}
endmodule

module ALU_control (
  input  [1:0] ALUOp,
  input  [5:0] Funct,
  output [3:0] ALUctrl,
  output RegtoPC
);

  // PLA ALU_ctrl: pin names not known; wires that end beside it: {ALUOp, Funct}
endmodule

module Registers (
  input  [31:0] Write_data,
  input  [4:0] Write_register,
  input  [4:0] Read_register_1,
  input  [4:0] Read_register_2,
  input  RegWrite,
  output [31:0] Read_data_1,
  output [31:0] Read_data_2
);

  // RegisterFile registerfile_1: pin names not known; wires that end beside it: Write_data, RegWrite, Write_register, Read_register_1, Read_register_2, Read_data_1, Read_data_2
endmodule

module Add (
  input  [31:0] Number,
  input  [31:0] Result,
  input  [31:0] Amount
);

  // MIPS_ALU mips_alu_1: pin names not known; wires that end beside it: Number, Amount, 4'b0010, Result
endmodule
