// Logisim project file_martin.circ as structural Verilog: 5 circuits, main circuit main
module main (
);

  wire mips_alu_1_p3, mips_alu_2_p5, not_1_out, undriven;
  wire [4:0] multiplexer_2_out_2, multiplexer_3_out;
  wire [5:0] instr__0_5;
  wire [27:0] shifter_2_out;
  wire [31:0] bit_extender_1_out, mips_alu_2_p1, mips_alu_2_p4, multiplexer_1_out, multiplexer_4_out,
       multiplexer_5_out, multiplexer_6_out, ram_1_data, register_1_q, registers_1_read_data_1,
       registers_1_read_data_2, shifter_1_out, shifter_3_out, undriven_2, undriven_3;
  wire [31:6] multiplexer_2_out;

  Register #(.width(32)) register_1 (.D(multiplexer_6_out), .en(undriven), .Q(register_1_q));  // open: clk, clr
  Multiplexer #(.width(32), .enable("false")) multiplexer_1 (
    .in0(undriven_2), .in1(shifter_1_out), .out(multiplexer_1_out), .sel(undriven));
  Shifter #(.width(32), .shift("lr")) shifter_1 (.in(register_1_q), .\dist (5'b00010), .out(shifter_1_out));
  RAM #(.addrWidth(24), .dataWidth(32), .bus("separate")) ram_1 (
    .addr(multiplexer_1_out[23:0]), .din(undriven_3), .data(ram_1_data));  // open: str, sel, clk, ld, clr
  Add add_1 (.Number(register_1_q), .Amount(32'h4), .Result(mips_alu_2_p1));
  Multiplexer #(.width(32), .enable("false")) multiplexer_2 (
    .in0({32{1'b0}}), .in1(ram_1_data),
    .out({multiplexer_2_out[31:21], multiplexer_2_out_2, multiplexer_2_out[15:6], instr__0_5}), .sel(undriven));
  Control control_1 (.Instruction_31_26(multiplexer_2_out[31:26]));  // open: RegDst, ALUsrc, MemtoReg, RegWrite, MemRead, MemWrite, Branch, ALUOp, Jump, ZeroInvert
  Shifter #(.width(28)) shifter_2 (
    .in({2'b00, multiplexer_2_out[25:21], multiplexer_2_out_2, multiplexer_2_out[15:6], instr__0_5}),
    .\dist (5'b00010), .out(shifter_2_out));
  Multiplexer #(.width(5), .enable("false")) multiplexer_3 (
    .in0(multiplexer_2_out[15:11]), .in1(multiplexer_2_out_2), .out(multiplexer_3_out));  // open: sel
  assign bit_extender_1_out = {{16{multiplexer_2_out[15]}}, {multiplexer_2_out[15:6], instr__0_5}};  // Bit_Extender bit_extender_1
  Registers registers_1 (
    .Read_data_1(registers_1_read_data_1), .Read_data_2(registers_1_read_data_2));  // open: Write_data, Write_register, Read_register_1, Read_register_2, RegWrite
  Multiplexer #(.width(32), .enable("false")) multiplexer_4 (
    .in0(bit_extender_1_out), .in1(registers_1_read_data_2), .out(multiplexer_4_out));  // open: sel
  Shifter #(.width(32)) shifter_3 (.in(bit_extender_1_out), .\dist (5'b00010), .out(shifter_3_out));
  // MIPS_ALU mips_alu_1: pin names not known; wires that end beside it: registers_1_read_data_1, multiplexer_4_out, mips_alu_1_p3
  // MIPS_ALU mips_alu_2: pin names not known; wires that end beside it: mips_alu_2_p1, shifter_3_out, 4'b0010, mips_alu_2_p4, mips_alu_2_p5
  Multiplexer #(.width(32), .enable("false")) multiplexer_5 (
    .in0(mips_alu_2_p1), .in1(mips_alu_2_p4), .out(multiplexer_5_out));  // open: sel
  Multiplexer #(.width(32), .enable("false")) multiplexer_6 (
    .in0({mips_alu_2_p1[31:28], shifter_2_out}), .in1(multiplexer_5_out), .out(multiplexer_6_out),
    .sel(not_1_out));
  not not_1 (not_1_out, mips_alu_2_p5);

  // Notes on the sheet:
  //   PC
  //   Should Run Instruction
  //   addr from sw/lw
  //   data from sw
  //   32 bit instruction should come here
  //   Alu Control
  //   !Jump
endmodule

module Control (
  input  [5:0] Instruction_31_26,
  output RegDst,
  output ALUsrc,
  output MemtoReg,
  output RegWrite,
  output MemRead,
  output MemWrite,
  output Branch,
  output [1:0] ALUOp,
  output Jump,
  output ZeroInvert
);

  // PLA Control: pin names not known; wires that end beside it: Instruction_31_26, {ZeroInvert, Jump, RegDst, ALUsrc, MemtoReg, RegWrite, MemRead, MemWrite, Branch, ALUOp}
endmodule

module ALU_control (
  input  [1:0] ALUOp,
  input  [5:0] Funct,
  output [3:0] ALUctrl,
  output RegtoPC
);

  // PLA ALU_ctrl: pin names not known; wires that end beside it: {ALUOp, Funct}
endmodule

module Registers (
  input  [31:0] Write_data,
  input  [4:0] Write_register,
  input  [4:0] Read_register_1,
  input  [4:0] Read_register_2,
  input  RegWrite,
  output [31:0] Read_data_1,
  output [31:0] Read_data_2
);

  // RegisterFile registerfile_1: pin names not known; wires that end beside it: Write_data, RegWrite, Write_register, Read_register_1, Read_register_2, Read_data_1, Read_data_2
endmodule

module Add (
  input  [31:0] Number,
  input  [31:0] Result,
  input  [31:0] Amount
);

  // MIPS_ALU mips_alu_1: pin names not known; wires that end beside it: Number, Amount, 4'b0010, Result
endmodule
